// Digital circuit 1bit_full_adder.dig as structural Verilog
module _1bit_full_adder (
  input  A,
  input  B,
  input  Cin,
  output Sum,
  output Cout
);

  wire and_1_out, and_2_out, and_3_out, and_4_out, and_5_out, and_6_out, and_7_out, and_8_out, and_9_out,
       and_10_out, and_11_out, not_1_out, not_2_out, not_3_out, or_1_out, or_3_out, or_4_out;

  not not_1 (not_1_out, A);
  not not_2 (not_2_out, B);
  not not_3 (not_3_out, Cin);
  and and_1 (and_1_out, A, B);
  and and_2 (and_2_out, A, Cin);
  and and_3 (and_3_out, B, Cin);
  and and_4 (and_4_out, A, not_2_out);
  and and_5 (and_5_out, not_1_out, B);
  and and_6 (and_6_out, not_1_out, not_2_out);
  and and_7 (and_7_out, A, B);
  or or_1 (or_1_out, and_1_out, and_2_out);
  and and_8 (and_8_out, and_4_out, not_3_out);
  and and_9 (and_9_out, and_5_out, not_3_out);
  and and_10 (and_10_out, and_6_out, Cin);
  and and_11 (and_11_out, and_7_out, Cin);
  or or_2 (Cout, or_1_out, and_3_out);
  or or_3 (or_3_out, and_8_out, and_9_out);
  or or_4 (or_4_out, and_10_out, and_11_out);
  or or_5 (Sum, or_3_out, or_4_out);
endmodule
