// Digital circuit 4bit_full_adder.dig as structural Verilog
module _4bit_full_adder (
  input  [3:0] A,
  input  [3:0] B,
  input  Control,
  output [3:0] Sum,
  output Carry_Out
);

  wire _1bit_full_adder_1_cout, _1bit_full_adder_2_cout, _1bit_full_adder_3_cout;

  _1bit_full_adder _1bit_full_adder_1 (.A(A[0]), .B(B[0]), .Cin(Control), .Sum(Sum[0]), .Cout(_1bit_full_adder_1_cout));
  _1bit_full_adder _1bit_full_adder_2 (
    .A(A[1]), .B(B[1]), .Cin(_1bit_full_adder_1_cout), .Sum(Sum[1]), .Cout(_1bit_full_adder_2_cout));
  _1bit_full_adder _1bit_full_adder_3 (
    .A(A[2]), .B(B[2]), .Cin(_1bit_full_adder_2_cout), .Sum(Sum[2]), .Cout(_1bit_full_adder_3_cout));
  _1bit_full_adder _1bit_full_adder_4 (
    .A(A[3]), .B(B[3]), .Cin(_1bit_full_adder_3_cout), .Sum(Sum[3]), .Cout(Carry_Out));
endmodule
