// Digital circuit 4bit_subtractor.dig as structural Verilog
module _4bit_subtractor (
  input  [3:0] A,
  input  [3:0] B,
  input  Control,
  output [3:0] Difference,
  output Carry_Out
);

  wire _1bit_full_adder_1_cout, _1bit_full_adder_2_cout, _1bit_full_adder_3_cout, xor_1_out, xor_2_out,
       xor_3_out, xor_4_out;

  xor xor_1 (xor_1_out, Control, B[0]);
  xor xor_2 (xor_2_out, Control, B[1]);
  xor xor_3 (xor_3_out, Control, B[2]);
  xor xor_4 (xor_4_out, Control, B[3]);
  _1bit_full_adder _1bit_full_adder_1 (
    .A(A[0]), .B(xor_1_out), .Cin(Control), .Sum(Difference[0]), .Cout(_1bit_full_adder_1_cout));
  _1bit_full_adder _1bit_full_adder_2 (
    .A(A[1]), .B(xor_2_out), .Cin(_1bit_full_adder_1_cout), .Sum(Difference[1]),
    .Cout(_1bit_full_adder_2_cout));
  _1bit_full_adder _1bit_full_adder_3 (
    .A(A[2]), .B(xor_3_out), .Cin(_1bit_full_adder_2_cout), .Sum(Difference[2]),
    .Cout(_1bit_full_adder_3_cout));
  _1bit_full_adder _1bit_full_adder_4 (
    .A(A[3]), .B(xor_4_out), .Cin(_1bit_full_adder_3_cout), .Sum(Difference[3]), .Cout(Carry_Out));
endmodule
